// Logisim project ex5.circ as structural Verilog: 5 circuits, main circuit RotRight
module RotRight (
  input  [15:0] INPUT0,
  input  [3:0] AMOUNT,
  output [15:0] OUTPUT0
);

  wire not_1_out, not_2_out, not_3_out, not_4_out;
  wire [15:0] multiplexer_1_out, multiplexer_2_out, multiplexer_3_out, rot1_1_out_2, rot2_1_out_2,
       rot4_1_out_2, rot8_1_out_2;

  rot8 rot8_1 (.out_2(rot8_1_out_2), .in_1(INPUT0));
  Multiplexer #(.enable("false"), .width(16)) multiplexer_1 (
    .in0(rot8_1_out_2), .in1(INPUT0), .out(multiplexer_1_out), .sel(not_1_out));
  not not_1 (not_1_out, AMOUNT[3]);
  not not_2 (not_2_out, AMOUNT[2]);
  not not_3 (not_3_out, AMOUNT[1]);
  rot4 rot4_1 (.out_2(rot4_1_out_2), .in_1(multiplexer_1_out));
  Multiplexer #(.enable("false"), .width(16)) multiplexer_2 (
    .in0(rot4_1_out_2), .in1(multiplexer_1_out), .out(multiplexer_2_out), .sel(not_2_out));
  not not_4 (not_4_out, AMOUNT[0]);
  rot2 rot2_1 (.out_2(rot2_1_out_2), .in_1(multiplexer_2_out));
  Multiplexer #(.enable("false"), .width(16)) multiplexer_3 (
    .in0(rot2_1_out_2), .in1(multiplexer_2_out), .out(multiplexer_3_out), .sel(not_3_out));
  rot1 rot1_1 (.out_2(rot1_1_out_2), .in_1(multiplexer_3_out));
  Multiplexer #(.enable("false"), .width(16)) multiplexer_4 (
    .in0(rot1_1_out_2), .in1(multiplexer_3_out), .out(OUTPUT0), .sel(not_4_out));
endmodule

module rot1 (
  input  [15:0] in_1,
  output [15:0] out_2
);


  assign out_2 = {in_1[0], in_1[15:1]};
endmodule

module rot2 (
  input  [15:0] in_1,
  output [15:0] out_2
);

  wire [15:0] rot1_1_out_2;

  rot1 rot1_1 (.out_2(rot1_1_out_2), .in_1(in_1));
  rot1 rot1_2 (.out_2(out_2), .in_1(rot1_1_out_2));
endmodule

module rot4 (
  input  [15:0] in_1,
  output [15:0] out_2
);

  wire [15:0] rot2_1_out_2;

  rot2 rot2_1 (.out_2(rot2_1_out_2), .in_1(in_1));
  rot2 rot2_2 (.out_2(out_2), .in_1(rot2_1_out_2));
endmodule

module rot8 (
  input  [15:0] in_1,
  output [15:0] out_2
);

  wire [15:0] rot4_1_out_2;

  rot4 rot4_1 (.out_2(rot4_1_out_2), .in_1(in_1));
  rot4 rot4_2 (.out_2(out_2), .in_1(rot4_1_out_2));
endmodule
