// Logisim project control-logic.circ as structural Verilog: 1 circuit, main circuit control_logic
module control_logic (
  input  [31:0] inst,
  input  BrEq,
  input  BrLt,
  output PCSel,
  output RegWEn,
  output [2:0] ImmSel,
  output BrUn,
  output ASel,
  output BSel,
  output [3:0] ALUSel,
  output MemRW,
  output [1:0] WBSel,
  output CSRSel,
  output CSRWen
);

  wire Add, Addi, And0, and_7_out, and_8_out, and_9_out, and_10_out, and_11_out, and_12_out, Andi, Auipc,
       Beq, Bge, Bgeu, Blt, Bltu, Bne, BType, comparator_1_eq, comparator_12_eq, comparator_13_eq,
       comparator_14_eq, comparator_15_eq, comparator_16_eq, comparator_17_eq, comparator_18_eq,
       comparator_19_eq, comparator_20_eq, Csrw, Csrwi, demultiplexer_1_out5, demultiplexer_2_out0,
       demultiplexer_2_out1, demultiplexer_2_out5, I, ICsr, IImm, IImmWrite, ILoad, ILoadWB, Jal, Jalr,
       JumpWrite, Lb, Lh, Lui, Lw, Mul, Mulh, Mulhu, not_1_out, not_2_out, not_3_out, Or0, or_1_out,
       or_11_out, or_14_out, or_15_out, or_16_out, or_17_out, or_18_out, or_19_out, or_20_out, Ori, RType,
       Sb, Sh, Sll0, Slli, Slt, Slti, Sra0, Srai, Srl0, Srli, SType, Sub, Sw, U, UWrite, Xor0, Xori;
  wire [1:0] bit_extender_4_out, IImmWB, JWB, multiplexer_1_out, or_5_out, RTypeWB, UTypeWB;

  Comparator #(.width(12)) comparator_1 (.a(inst[31:20]), .b(12'h51e), .eq(comparator_1_eq));  // open: gt, lt
  or or_1 (or_1_out, Csrw, Csrwi);
  assign RTypeWB = {{1{1'b0}}, BSel};  // Bit_Extender bit_extender_1
  assign IImmWB = {{1{1'b0}}, IImmWrite};  // Bit_Extender bit_extender_2
  assign UTypeWB = {{1{1'b0}}, UWrite};  // Bit_Extender bit_extender_3
  Comparator #(.width(7)) comparator_2 (.a(inst[6:0]), .b(7'b0110011), .eq(RType));  // open: gt, lt
  Comparator #(.width(7)) comparator_3 (.a(inst[6:0]), .b(7'b0000011), .eq(ILoad));  // open: gt, lt
  Comparator #(.width(7)) comparator_4 (.a(inst[6:0]), .b(7'b0010011), .eq(IImm));  // open: gt, lt
  Comparator #(.width(7)) comparator_5 (.a(inst[6:0]), .b(7'b1100111), .eq(Jalr));  // open: gt, lt
  Comparator #(.width(7)) comparator_6 (.a(inst[6:0]), .b(7'b1110011), .eq(ICsr));  // open: gt, lt
  Comparator #(.width(7)) comparator_7 (.a(inst[6:0]), .b(7'b0100011), .eq(SType));  // open: gt, lt
  Comparator #(.width(7)) comparator_8 (.a(inst[6:0]), .b(7'b1100011), .eq(BType));  // open: gt, lt
  Comparator #(.width(7)) comparator_9 (.a(inst[6:0]), .b(7'b0010111), .eq(Auipc));  // open: gt, lt
  Comparator #(.width(7)) comparator_10 (.a(inst[6:0]), .b(7'b0110111), .eq(Lui));  // open: gt, lt
  Comparator #(.width(7)) comparator_11 (.a(inst[6:0]), .b(7'b1101111), .eq(Jal));  // open: gt, lt
  or or_2 (I, ILoad, IImm, Jalr, ICsr);
  or or_3 (U, Auipc, Lui);
  Priority_Encoder priority_encoder_1 (
    .in0(I), .in1(SType), .in2(BType), .in3(U), .in4(Jal), .out(ImmSel));  // open: in5, in6, in7, en_in, gs, en_out
  or or_4 (BrUn, Bltu, Bgeu);
  Priority_Encoder #(.select(1)) priority_encoder_2 (.in0(Csrw), .in1(Csrwi), .out(CSRSel));  // open: gs, en_out, en_in
  and and_1 (CSRWen, comparator_1_eq, or_1_out);
  assign or_5_out = RTypeWB | IImmWB | UTypeWB | JWB;  // OR_Gate or_5, 2 bits wide
  Multiplexer #(.enable("false"), .width(2)) multiplexer_1 (
    .in1(2'b00), .out(multiplexer_1_out), .sel(ILoadWB));  // open: in0
  assign bit_extender_4_out = {{1{1'b0}}, JumpWrite};  // Bit_Extender bit_extender_4
  Shifter #(.width(2)) shifter_1 (.in(bit_extender_4_out), .\dist (1'b1), .out(JWB));
  Demultiplexer #(.enable("false"), .select(3)) demultiplexer_1 (
    .out0(Addi), .out1(Slli), .out2(Slti), .out4(Xori), .out5(demultiplexer_1_out5), .out6(Ori), .out7(Andi),
    .in(IImm), .sel(inst[14:12]));  // open: out3
  Multiplexer #(.enable("false"), .width(2)) multiplexer_2 (
    .in0(or_5_out), .in1(multiplexer_1_out), .out(WBSel), .sel(ILoadWB));
  Demultiplexer #(.enable("false"), .select(3)) demultiplexer_2 (
    .out0(demultiplexer_2_out0), .out1(demultiplexer_2_out1), .out2(Slt), .out3(Mulhu), .out4(Xor0),
    .out5(demultiplexer_2_out5), .out6(Or0), .out7(And0), .in(RType), .sel(inst[14:12]));
  Comparator #(.width(7)) comparator_12 (.a(inst[31:25]), .b({7{1'b0}}), .eq(comparator_12_eq));  // open: gt, lt
  Comparator #(.width(7)) comparator_13 (.a(inst[31:25]), .b(7'b0000001), .eq(comparator_13_eq));  // open: gt, lt
  Comparator #(.width(7)) comparator_14 (.a(inst[31:25]), .b(7'b0100000), .eq(comparator_14_eq));  // open: gt, lt
  or or_6 (BSel, Add, Mul, Sub, Sll0, Mulh, Mulhu, Slt, Xor0, Srl0, Sra0, Or0, And0);
  or or_7 (IImmWrite, Addi, Slli, Slti, Xori, Srli, Srai, Ori, Andi);
  not not_1 (not_1_out, BrEq);
  not not_2 (not_2_out, BrLt);
  not not_3 (not_3_out, BrLt);
  Demultiplexer #(.enable("false"), .select(3)) demultiplexer_3 (
    .out1(Csrw), .out5(Csrwi), .in(ICsr), .sel(inst[14:12]));  // open: out0, out2, out3, out4, out6, out7
  and and_2 (Srli, demultiplexer_1_out5, comparator_15_eq);
  Comparator #(.width(7)) comparator_15 (.a(inst[31:25]), .b({7{1'b0}}), .eq(comparator_15_eq));  // open: gt, lt
  and and_3 (Srai, demultiplexer_1_out5, comparator_16_eq);
  Comparator #(.width(7)) comparator_16 (.a(inst[31:25]), .b(7'b0100000), .eq(comparator_16_eq));  // open: gt, lt
  and and_4 (Add, demultiplexer_2_out0, comparator_12_eq);
  and and_5 (Mul, demultiplexer_2_out0, comparator_13_eq);
  and and_6 (Sub, demultiplexer_2_out0, comparator_14_eq);
  or or_8 (JumpWrite, Jalr, Jal);
  or or_9 (ILoadWB, Lb, Lh, Lw);
  or or_10 (MemRW, Sb, Sh, Sw);
  and and_7 (and_7_out, BrEq, Beq);
  and and_8 (and_8_out, not_1_out, Bne);
  and and_9 (and_9_out, BrLt, Blt);
  and and_10 (and_10_out, not_2_out, Bge);
  and and_11 (and_11_out, BrLt, Bltu);
  and and_12 (and_12_out, not_3_out, Bgeu);
  or or_11 (or_11_out, Jalr, Jal);
  or or_12 (UWrite, Auipc, Lui);
  or or_13 (PCSel, and_7_out, and_8_out, and_9_out, and_10_out, and_11_out, and_12_out, or_11_out);
  Demultiplexer #(.enable("false"), .select(3)) demultiplexer_4 (
    .out0(Lb), .out1(Lh), .out2(Lw), .in(ILoad), .sel(inst[14:12]));  // open: out3, out4, out5, out6, out7
  Demultiplexer #(.enable("false"), .select(3)) demultiplexer_5 (
    .out0(Sb), .out1(Sh), .out2(Sw), .in(SType), .sel(inst[14:12]));  // open: out3, out4, out5, out6, out7
  Comparator #(.width(7)) comparator_17 (.a(inst[31:25]), .b({7{1'b0}}), .eq(comparator_17_eq));  // open: gt, lt
  Comparator #(.width(7)) comparator_18 (.a(inst[31:25]), .b(7'b0000001), .eq(comparator_18_eq));  // open: gt, lt
  and and_13 (Sll0, demultiplexer_2_out1, comparator_17_eq);
  and and_14 (Mulh, demultiplexer_2_out1, comparator_18_eq);
  Comparator #(.width(7)) comparator_19 (.a(inst[31:25]), .b({7{1'b0}}), .eq(comparator_19_eq));  // open: gt, lt
  Comparator #(.width(7)) comparator_20 (.a(inst[31:25]), .b(7'b0100000), .eq(comparator_20_eq));  // open: gt, lt
  or or_14 (or_14_out, Slli, Sll0);
  or or_15 (or_15_out, Slti, Slt);
  or or_16 (or_16_out, Xori, Xor0);
  or or_17 (or_17_out, Srli, Srl0);
  or or_18 (or_18_out, Ori, Or0);
  or or_19 (or_19_out, Andi, And0);
  or or_20 (or_20_out, Srai, Sra0);
  or or_21 (RegWEn, BSel, ILoadWB, IImmWrite, UWrite, JumpWrite);
  or or_22 (ASel, Beq, Bne, Blt, Bge, Bltu, Bgeu, Auipc, Jal);
  Demultiplexer #(.enable("false"), .select(3)) demultiplexer_6 (
    .out0(Beq), .out1(Bne), .out4(Blt), .out5(Bge), .out6(Bltu), .out7(Bgeu), .in(BType), .sel(inst[14:12]));  // open: out2, out3
  and and_15 (Srl0, demultiplexer_2_out5, comparator_19_eq);
  and and_16 (Sra0, demultiplexer_2_out5, comparator_20_eq);
  Priority_Encoder #(.select(4)) priority_encoder_3 (
    .in0(1'b0), .in1(or_14_out), .in2(or_15_out), .in4(or_16_out), .in5(or_17_out), .in6(or_18_out),
    .in7(or_19_out), .in8(Mul), .in9(Mulh), .in11(Mulhu), .in12(Sub), .in13(or_20_out), .in15(Lui),
    .out(ALUSel));  // open: in3, in10, in14, gs, en_out, en_in

  // Other names for the same wires on the sheet: rs2[4:0] = inst[24:20]; funct7[6:0] = inst[31:25];
  //   ILoadWrite = ILoadWB; Opcode[6:0] = inst[6:0]; rd[4:0] = inst[11:7]; funct3[2:0] = inst[14:12];
  //   rs1[4:0] = inst[19:15]; RWrite = BSel

  // Notes on the sheet:
  //   Jalr
  //   Auipc
  //   Lui
  //   Jal
  //   ALU: 01
  //   ALU: 01
  //   ALU: 01
  //   PC+4: 2
  //   READ_DATA: 00
  //   INPUTS to your circuit
  //   DON'T CHANGE THE LOCATIONS OF THE INPUTS AND OUTPUTS!
  //   OUTPUT from your circuit
endmodule
