// Logisim project cpu.circ as structural Verilog: 1 circuit, main circuit cpu
module cpu (
  input  clk,
  input  [31:0] INSTRUCTION,
  input  [31:0] READ_DATA,
  output [31:0] WRITE_ADDRESS,
  output [31:0] PROGRAM_COUNTER,
  output [31:0] ra,
  output [31:0] sp,
  output [31:0] t0,
  output [31:0] t1,
  output [31:0] t2,
  output [31:0] s0,
  output [31:0] s1,
  output [31:0] a0,
  output [31:0] tohost,
  output [3:0] WRITE_ENABLE,
  output [31:0] WRITE_DATA
);

  wire ASel, BrEq, BrLt, BrUn, BSel, comparator_1_eq, CSRSel, CSRWen, MemRW, PCSel, RegWEn;
  wire [1:0] bhw, WBSel;
  wire [2:0] ImmSel;
  wire [2:2] funct3;
  wire [3:0] ALUSel, multiplexer_6_out, shifter_1_out;
  wire [4:0] bit_extender_2_out;
  wire [6:0] funct7;
  wire [7:0] multiplexer_11_out, multiplexer_11_out_3;
  wire [15:0] multiplexer_11_out_2;
  wire [24:0] InstP;
  wire [31:0] adder_1_out, bit_extender_1_out, bit_extender_3_out, bit_extender_4_out, immValue,
       multiplexer_1_out, multiplexer_2_out, multiplexer_3_out, multiplexer_4_out, multiplexer_5_out,
       multiplexer_9_out, multiplexer_10_out, multiplexer_12_out, multiplexer_13_out, multiplexer_15_out, PC,
       PC_Plus4, ReadData1, ReadData2, shifter_2_out, shifter_3_out, shifter_4_out, shifter_5_out,
       shifter_6_out, shifter_7_out, shifter_8_out, shifter_9_out, shifter_10_out, shifter_11_out,
       shifter_12_out, undriven, WriteBack;

  Adder #(.width(32)) adder_1 (.a(PROGRAM_COUNTER), .b(32'h4), .out(adder_1_out));  // open: cin, cout
  Multiplexer #(.enable("false"), .width(32)) multiplexer_1 (
    .in0(INSTRUCTION), .in1(32'h13), .out(multiplexer_1_out), .sel(PCSel));
  Multiplexer #(.enable("false"), .width(32)) multiplexer_2 (
    .in0(adder_1_out), .in1(WRITE_ADDRESS), .out(multiplexer_2_out), .sel(PCSel));
  Register #(.width(32)) register_1 (
    .D(multiplexer_1_out), .clk(clk), .Q({funct7, InstP[24:15], funct3[2], bhw, InstP[11:0]}));  // open: en, clr
  Register #(.width(32)) u_PC (.D(multiplexer_2_out), .clk(clk), .Q(PROGRAM_COUNTER));  // open: en, clr
  Register #(.width(32)) register_2 (.D(PROGRAM_COUNTER), .clk(clk), .Q(PC));  // open: en, clr
  control_logic control_logic_1 (
    .CSRWen(CSRWen), .PCSel(PCSel), .RegWEn(RegWEn), .ImmSel(ImmSel), .BrUn(BrUn), .ASel(ASel), .BSel(BSel),
    .ALUSel(ALUSel), .MemRW(MemRW), .WBSel(WBSel), .CSRSel(CSRSel),
    .inst({funct7, InstP[24:15], funct3[2], bhw, InstP[11:0]}), .BrEq(BrEq), .BrLt(BrLt));
  Adder #(.width(32)) adder_2 (.a(PC), .b(32'h4), .out(PC_Plus4));  // open: cin, cout
  imm_gen imm_gen_1 (.inst({funct7, InstP[24:15], funct3[2], bhw, InstP[11:0]}), .ImmSel(ImmSel), .imm(immValue));
  regfile regfile_1 (
    .rs1(InstP[19:15]), .rs2(InstP[24:20]), .rd(InstP[11:7]), .Write_Data(WriteBack), .RegWEn(RegWEn),
    .clk(clk), .ra(ra), .sp(sp), .t0(t0), .t1(t1), .t2(t2), .s0(s0), .s1(s1), .a0(a0),
    .Read_Data_1(ReadData1), .Read_Data_2(ReadData2));
  assign bit_extender_1_out = {{27{1'b0}}, InstP[19:15]};  // Bit_Extender bit_extender_1
  Multiplexer #(.enable("false"), .width(32)) multiplexer_3 (
    .in0(ReadData1), .in1(PC), .out(multiplexer_3_out), .sel(ASel));
  Multiplexer #(.enable("false"), .width(32)) multiplexer_4 (
    .in0(immValue), .in1(ReadData2), .out(multiplexer_4_out), .sel(BSel));
  Multiplexer #(.enable("false"), .width(32)) multiplexer_5 (
    .in0(ReadData1), .in1(bit_extender_1_out), .out(multiplexer_5_out), .sel(CSRSel));
  alu alu_1 (.Result(WRITE_ADDRESS), .A(multiplexer_3_out), .B(multiplexer_4_out), .ALUSel(ALUSel));
  branch_comp branch_comp_1 (.rs1(ReadData1), .rs2(ReadData2), .BrUn(BrUn), .BrEq(BrEq), .BrLt(BrLt));
  Multiplexer #(.enable("false"), .select(2), .width(4)) multiplexer_6 (
    .in0(4'b0001), .in1(4'b0011), .in2(4'b1111), .out(multiplexer_6_out), .sel(bhw));  // open: in3
  // csr csr_1: pin names not known; wires that end beside it: {funct7, InstP[24:20]}, multiplexer_5_out, CSRWen, clk, tohost
  assign bit_extender_2_out = {{3{1'b0}}, WRITE_ADDRESS[1:0]};  // Bit_Extender bit_extender_2
  Multiplexer #(.enable("false"), .width(4)) multiplexer_7 (
    .in0(4'b0000), .in1(shifter_1_out), .out(WRITE_ENABLE), .sel(MemRW));
  Shifter #(.width(4)) shifter_1 (.in(multiplexer_6_out), .\dist (WRITE_ADDRESS[1:0]), .out(shifter_1_out));
  Shifter #(.width(32)) shifter_2 (.in(undriven), .\dist (bit_extender_2_out), .out(shifter_2_out));
  Multiplexer #(.enable("false"), .width(32)) multiplexer_8 (
    .in0(undriven), .in1(shifter_2_out), .sel(comparator_1_eq));  // open: out
  Comparator #(.width(7)) comparator_1 (.a(InstP[6:0]), .b(7'b0000011), .eq(comparator_1_eq));  // open: gt, lt
  Shifter #(.shift("lr"), .width(32)) shifter_3 (.in(READ_DATA), .\dist (5'b01000), .out(shifter_3_out));
  Shifter #(.shift("lr"), .width(32)) shifter_4 (.in(READ_DATA), .\dist (5'b10000), .out(shifter_4_out));
  Shifter #(.shift("lr"), .width(32)) shifter_5 (.in(READ_DATA), .\dist (5'b11000), .out(shifter_5_out));
  Multiplexer #(.enable("false"), .select(2), .width(32)) multiplexer_9 (
    .in0(READ_DATA), .in1(shifter_3_out), .in2(shifter_4_out), .in3(shifter_5_out), .out(multiplexer_9_out),
    .sel(WRITE_ADDRESS[1:0]));
  Shifter #(.shift("lr"), .width(32)) shifter_6 (.in(READ_DATA), .\dist (5'b01000), .out(shifter_6_out));
  Shifter #(.shift("lr"), .width(32)) shifter_7 (.in(READ_DATA), .\dist (5'b10000), .out(shifter_7_out));
  Multiplexer #(.enable("false"), .select(2), .width(32)) multiplexer_10 (
    .in0(READ_DATA), .in1(shifter_6_out), .in2(shifter_7_out), .out(multiplexer_10_out),
    .sel(WRITE_ADDRESS[1:0]));  // open: in3
  Multiplexer #(.enable("false"), .select(2), .width(32)) multiplexer_11 (
    .in0(multiplexer_9_out), .in1(multiplexer_10_out), .in2(READ_DATA),
    .out({multiplexer_11_out_3, multiplexer_11_out_2, multiplexer_11_out}), .sel(bhw));  // open: in3
  Shifter #(.width(32)) shifter_8 (.in(ReadData2), .\dist (5'b01000), .out(shifter_8_out));
  Shifter #(.width(32)) shifter_9 (.in(ReadData2), .\dist (5'b10000), .out(shifter_9_out));
  Shifter #(.width(32)) shifter_10 (.in(ReadData2), .\dist (5'b11000), .out(shifter_10_out));
  Shifter #(.width(32)) shifter_11 (.in(ReadData2), .\dist (5'b01000), .out(shifter_11_out));
  Shifter #(.width(32)) shifter_12 (.in(ReadData2), .\dist (5'b10000), .out(shifter_12_out));
  Multiplexer #(.enable("false"), .select(2), .width(32)) multiplexer_12 (
    .in0(ReadData2), .in1(shifter_8_out), .in2(shifter_9_out), .in3(shifter_10_out),
    .out(multiplexer_12_out), .sel(WRITE_ADDRESS[1:0]));
  Multiplexer #(.enable("false"), .select(2), .width(32)) multiplexer_13 (
    .in0(ReadData2), .in1(shifter_11_out), .in2(shifter_12_out), .out(multiplexer_13_out),
    .sel(WRITE_ADDRESS[1:0]));  // open: in3
  assign bit_extender_3_out = {{24{multiplexer_11_out[7]}}, multiplexer_11_out};  // Bit_Extender bit_extender_3
  assign bit_extender_4_out = {{16{multiplexer_11_out_2[7]}}, {multiplexer_11_out_2[7:0], multiplexer_11_out}};  // Bit_Extender bit_extender_4
  Multiplexer #(.enable("false"), .select(2), .width(32)) multiplexer_14 (
    .in0(multiplexer_12_out), .in1(multiplexer_13_out), .in2(ReadData2), .out(WRITE_DATA), .sel(bhw));  // open: in3
  Multiplexer #(.enable("false"), .select(2), .width(32)) multiplexer_15 (
    .in0(bit_extender_3_out), .in1(bit_extender_4_out),
    .in2({multiplexer_11_out_3, multiplexer_11_out_2, multiplexer_11_out}), .out(multiplexer_15_out),
    .sel(bhw));  // open: in3
  Multiplexer #(.enable("false"), .select(2), .width(32)) multiplexer_16 (
    .in0(multiplexer_15_out), .in1(WRITE_ADDRESS), .in2(PC_Plus4), .out(WriteBack), .sel(WBSel));  // open: in3

  // Other names for the same wires on the sheet: rs2[4:0] = InstP[24:20];
  //   InstP (some bits) = {funct7, funct3[2], bhw}; ALUResult[31:0] = WRITE_ADDRESS; Offset[1:0] = WRITE_ADDRESS[1:0];
  //   Opcode[6:0] = InstP[6:0]; rd[4:0] = InstP[11:7]; funct3[1:0] = bhw; rs1[4:0] = InstP[19:15]

  // Notes on the sheet:
  //   Output to IMEM
  //   IMEM (do **NOT** move this)
  //   Inputs from IMEM
  //   It is OK to move the PC, RegFile, ALU, MEM, Branch Comp, Imm Gen, and Control Logic to wherever is most convenient for you when constructing your CPU, and to delete this text
  //   Inputs/Outputs for testing. Do **NOT** move these.
  //   Outputs To DMEM
  //   DMEM (do **NOT** move this)
  //   Inputs From DMEM
endmodule
