// Logisim project regfile.circ as structural Verilog: 1 circuit, main circuit regfile
module regfile (
  input  [4:0] rs1,
  input  [4:0] rs2,
  input  [4:0] rd,
  input  [31:0] Write_Data,
  input  RegWEn,
  input  clk,
  output [31:0] ra,
  output [31:0] sp,
  output [31:0] t0,
  output [31:0] t1,
  output [31:0] t2,
  output [31:0] s0,
  output [31:0] s1,
  output [31:0] a0,
  output [31:0] Read_Data_1,
  output [31:0] Read_Data_2
);

  wire wa0, wra, ws0, ws1, wsp, wt0, wt1, wt2, wx0, wx3, wx4, wx11, wx12, wx13, wx14, wx15, wx16, wx17, wx18,
       wx19, wx20, wx21, wx22, wx23, wx24, wx25, wx26, wx27, wx28, wx29, wx30, wx31;
  wire [31:0] x0, x3, x4, x11, x12, x13, x14, x15, x16, x17, x18, x19, x20, x21, x22, x23, x24, x25, x26,
       x27, x28, x29, x30, x31;

  Demultiplexer #(.enable("false"), .select(5)) demultiplexer_1 (
    .out0(wx0), .out1(wra), .out2(wsp), .out3(wx3), .out4(wx4), .out5(wt0), .out6(wt1), .out7(wt2),
    .out8(ws0), .out9(ws1), .out10(wa0), .out11(wx11), .out12(wx12), .out13(wx13), .out14(wx14),
    .out15(wx15), .out16(wx16), .out17(wx17), .out18(wx18), .out19(wx19), .out20(wx20), .out21(wx21),
    .out22(wx22), .out23(wx23), .out24(wx24), .out25(wx25), .out26(wx26), .out27(wx27), .out28(wx28),
    .out29(wx29), .out30(wx30), .out31(wx31), .in(RegWEn), .sel(rd));
  Register #(.width(32)) register_1 (.D(Write_Data), .en(wx0), .clk(clk), .Q(x0), .clr(1'b1));
  Register #(.width(32)) register_2 (.D(Write_Data), .en(wt0), .clk(clk), .Q(t0));  // open: clr
  Register #(.width(32)) register_3 (.D(Write_Data), .en(ws0), .clk(clk), .Q(s0));  // open: clr
  Register #(.width(32)) register_4 (.D(Write_Data), .en(wra), .clk(clk), .Q(ra));  // open: clr
  Register #(.width(32)) register_5 (.D(Write_Data), .en(wt1), .clk(clk), .Q(t1));  // open: clr
  Register #(.width(32)) register_6 (.D(Write_Data), .en(ws1), .clk(clk), .Q(s1));  // open: clr
  Multiplexer #(.enable("false"), .select(5), .width(32)) multiplexer_1 (
    .in0(x0), .in1(ra), .in2(sp), .in3(x3), .in4(x4), .in5(t0), .in6(t1), .in7(t2), .in8(s0), .in9(s1),
    .in10(a0), .in11(x11), .in12(x12), .in13(x13), .in14(x14), .in15(x15), .in16(x16), .in17(x17),
    .in18(x18), .in19(x19), .in20(x20), .in21(x21), .in22(x22), .in23(x23), .in24(x24), .in25(x25),
    .in26(x26), .in27(x27), .in28(x28), .in29(x29), .in30(x30), .in31(x31), .out(Read_Data_1), .sel(rs1));
  Register #(.width(32)) register_7 (.D(Write_Data), .en(wx0), .clk(clk), .Q(x3));  // open: clr
  Register #(.width(32)) register_8 (.D(Write_Data), .en(wx12), .clk(clk), .Q(x12));  // open: clr
  Register #(.width(32)) register_9 (.D(Write_Data), .en(wx15), .clk(clk), .Q(x15));  // open: clr
  Register #(.width(32)) register_10 (.D(Write_Data), .en(wx18), .clk(clk), .Q(x18));  // open: clr
  Register #(.width(32)) register_11 (.D(Write_Data), .en(wx21), .clk(clk), .Q(x21));  // open: clr
  Register #(.width(32)) register_12 (.D(Write_Data), .en(wx24), .clk(clk), .Q(x24));  // open: clr
  Register #(.width(32)) register_13 (.D(Write_Data), .en(wx27), .clk(clk), .Q(x27));  // open: clr
  Register #(.width(32)) register_14 (.D(Write_Data), .en(wx30), .clk(clk), .Q(x30));  // open: clr
  Register #(.width(32)) register_15 (.D(Write_Data), .en(wsp), .clk(clk), .Q(sp));  // open: clr
  Register #(.width(32)) register_16 (.D(Write_Data), .en(wt2), .clk(clk), .Q(t2));  // open: clr
  Register #(.width(32)) register_17 (.D(Write_Data), .en(wa0), .clk(clk), .Q(a0));  // open: clr
  Register #(.width(32)) register_18 (.D(Write_Data), .en(wx4), .clk(clk), .Q(x4));  // open: clr
  Register #(.width(32)) register_19 (.D(Write_Data), .en(wx13), .clk(clk), .Q(x13));  // open: clr
  Register #(.width(32)) register_20 (.D(Write_Data), .en(wx16), .clk(clk), .Q(x16));  // open: clr
  Register #(.width(32)) register_21 (.D(Write_Data), .en(wx19), .clk(clk), .Q(x19));  // open: clr
  Register #(.width(32)) register_22 (.D(Write_Data), .en(wx22), .clk(clk), .Q(x22));  // open: clr
  Register #(.width(32)) register_23 (.D(Write_Data), .en(wx25), .clk(clk), .Q(x25));  // open: clr
  Register #(.width(32)) register_24 (.D(Write_Data), .en(wx28), .clk(clk), .Q(x28));  // open: clr
  Register #(.width(32)) register_25 (.D(Write_Data), .en(wx31), .clk(clk), .Q(x31));  // open: clr
  Multiplexer #(.enable("false"), .select(5), .width(32)) multiplexer_2 (
    .in0(x0), .in1(ra), .in2(sp), .in3(x3), .in4(x4), .in5(t0), .in6(t1), .in7(t2), .in8(s0), .in9(s1),
    .in10(a0), .in11(x11), .in12(x12), .in13(x13), .in14(x14), .in15(x15), .in16(x16), .in17(x17),
    .in18(x18), .in19(x19), .in20(x20), .in21(x21), .in22(x22), .in23(x23), .in24(x24), .in25(x25),
    .in26(x26), .in27(x27), .in28(x28), .in29(x29), .in30(x30), .in31(x31), .out(Read_Data_2), .sel(rs2));
  Register #(.width(32)) register_26 (.D(Write_Data), .en(wx11), .clk(clk), .Q(x11));  // open: clr
  Register #(.width(32)) register_27 (.D(Write_Data), .en(wx14), .clk(clk), .Q(x14));  // open: clr
  Register #(.width(32)) register_28 (.D(Write_Data), .en(wx17), .clk(clk), .Q(x17));  // open: clr
  Register #(.width(32)) register_29 (.D(Write_Data), .en(wx20), .clk(clk), .Q(x20));  // open: clr
  Register #(.width(32)) register_30 (.D(Write_Data), .en(wx23), .clk(clk), .Q(x23));  // open: clr
  Register #(.width(32)) register_31 (.D(Write_Data), .en(wx27), .clk(clk), .Q(x26));  // open: clr
  Register #(.width(32)) register_32 (.D(Write_Data), .en(wx29), .clk(clk), .Q(x29));  // open: clr

  // Other names for the same wires on the sheet: read_data1[31:0] = Read_Data_1; read_data2[31:0] = Read_Data_2;
  //   read_reg1[4:0] = rs1; read_reg2[4:0] = rs2; write_en = RegWEn; write_reg[4:0] = rd

  // Notes on the sheet:
  //   INPUTS to your circuit
  //   DON'T CHANGE THE LOCATIONS OF THE INPUTS AND OUTPUTS!
  //   These are DEBUG/TEST outputs from your circuit.
  //   OUTPUTS from your circuit
endmodule
